# Fritzing sketch Untitled Sketch (saved by Fritzing 0.9.10b)
breadboards: 1

parts:
  R1 = Resistor [tolerance=±5% power=0.25 resistance=330 package=THT]
  VCC1 = Battery block 9V
  LED1 = LED - 3mm [color="Orange (620nm)" current=30mA package="3 mm [THT]"]
  VM1 = Multimeter (DC Voltage)

nets:
  N1: R1.Pin_0, VCC1.+, VM1.V_Probe
  N2: R1.Pin_1, LED1.anode
  N3: VCC1.-, LED1.cathode, VM1.COM_Probe

notes:
  Led + Pi l +Simulation

// code stored in the sketch: Untitled.ino
void setup() {
  // put your setup code here, to run once:
  /*multiple*/


  // Digital 13 Pini Ç?k?? yapmak istiyorum
  pinMode(13, OUTPUT);  // ; unutma
}


void loop() {
  // put your main code here, to run repeatedly:
  digitalWrite(13, HIGH);  // Lambay? yak
  delay(2000);             // 2.saniye bekle
  digitalWrite(13, LOW);   // Lambay? söndür
  delay(1000);             // 1. saniye bekle(uyu)


  // Döngüyü 20 kez çal??s?n sonras?nda dursun.
  /*
  bool isFlag=true;
  for(int i=0; i<20; i++){
    if(i==20)
      break;
  }       
  */


  // Döngüyü 20 kez çal??s?n sonras?nda dursun.
  bool isFlag = true;
  for (int i = 0; i < 20 && isFlag; i++) {
    if (i == 20) {
      isFlag = false;
    }
  }
}
