# Fritzing sketch Untitled Sketch (saved by Fritzing 0.9.10b)

parts:
  Parça1 = Arduino Uno (Rev3)
  LED1 = LED - 5mm [color="Red (633nm)" current=0.030 package="5 mm [THT]"]
  R1 = Resistor [tolerance=±5% power=0.25 resistance=220 package=THT]

nets:
  N1: Parça1.GND, LED1.cathode
  N2: Parça1.D2, R1.Pin_1

// code stored in the sketch: Untitled.ino
void setup(){

// Digital pin seçmeliyim
pinMode(2,OUTPUT);
}



void loop(){
digitalWrite(2,HIGH);//lamba yan
delay(2000);
digitalWrite(2,LOW);// Lamba son
delay(1000);
}
