# Fritzing sketch Untitled Sketch 3 (saved by Fritzing 0.9.10b)
breadboards: 1

parts:
  Parça1 = Arduino Uno (Rev3)
  R1 = Resistor [tolerance=±5% power=0.25 resistance=220 package=THT]
  R2 = Resistor [tolerance=±5% power=0.25 resistance=220 package=THT]
  LED1 = LED - 5mm [color="Yellow (574nm)" current=0.030 package="5 mm [THT]"]
  LED2 = LED - 5mm [color="Blue (525nm)" current=0.030 package="5 mm [THT]"]

nets:
  N1: Parça1.D9_PWM, R1.Pin_1
  N2: Parça1.D12/MISO, R2.Pin_1
  N3: Parça1.GND, LED1.cathode, LED2.cathode
  N4: R1.Pin_0, LED2.anode
  N5: R2.Pin_0, LED1.anode

notes:
  GND=Siyah Kablo
  5V = Kırmızı Kablo

// code stored in the sketch: Untitled3.ino
void setup(){

// Sar? LED
pinMode(12,OUTPUT);

// Mavi LED
pinMode(9,OUTPUT);
}



void loop(){
// Mavi yans?n
digitalWrite(9,HIGH);
delay(500);

// Sar? Yans?n
digitalWrite(12,HIGH);
delay(1000);

// Mavi Sönsün
digitalWrite(9,LOW);
delay(1000);

// Sar? Sönsün
digitalWrite(12,LOW);
delay(1000);

}
