# Fritzing sketch Untitled Sketch 2 (saved by Fritzing 0.9.10b)
breadboards: 1

parts:
  R1 = Resistor [tolerance=±5% power=0.25 resistance=220 package=THT]
  R2 = Resistor [tolerance=±5% power=0.25 resistance=220 package=THT]
  LED1 = LED - 5mm [color="Blue (525nm)" current=30mA package="5 mm [THT]"]  # not connected
  S1 = Momentary Switch [package=ksa_sealed_tac_switch]
  Parça1 = Arduino Uno (Rev3)

nets:
  N1: R1.Pin_0, Parça1.D12/MISO
  N2: R2.Pin_0, S1.1, Parça1.D8
  N3: R2.Pin_1, Parça1.GND
  N4: S1.3, Parça1.5V

notes:
  Vcc(5V)= Kırmızı
  Gnd=Siyah
  Button: digital(8)
  Led:digital(12)

// code stored in the sketch: Untitled2.ino
#define Button 8
#define Led 12

void setup(){
// Led
// pinMode(12,OUTPUT);
pinMode(Led,OUTPUT);


// Button 
// pinMode(8,INPUT);
pinMode(Button,INPUT);

}


void loop(){

if(digitalRead(Button) == 1){
	delay(500);
	digitalWrite(Led,HIGH);
}else{

	digitalWrite(Led,LOW);
}

}
